// Digital circuit simple_circuit_with_mux.dig as structural Verilog
module simple_circuit_with_mux (
  input  in_a,
  input  in_b,
  input  in_c,
  input  in_x,
  input  in_y,
  input  in_z,
  input  mux_sel,
  output out_q
);

  wire and_1_out, not_1_out, not_2_out, or_1_out, or_2_out, xor_1_out;

  not not_1 (not_1_out, in_a);
  xor xor_1 (xor_1_out, in_x, in_y);
  not not_2 (not_2_out, in_z);
  and and_1 (and_1_out, not_1_out, in_b);
  or or_1 (or_1_out, xor_1_out, not_2_out);
  or or_2 (or_2_out, and_1_out, in_c);
  Multiplexer multiplexer_1 (.sel(mux_sel), .in_0(or_2_out), .in_1(or_1_out), .out(out_q));
endmodule
