// Digital circuit fulladder.dig as structural Verilog
module fulladder (
  input  a_i,
  input  b_i,
  input  carry_i,
  output sum_o,
  output carry_o
);

  wire and_1_out, and_2_out, xor_1_out;

  xor xor_1 (xor_1_out, a_i, b_i);
  and and_1 (and_1_out, a_i, b_i);
  and and_2 (and_2_out, xor_1_out, carry_i);
  xor xor_2 (sum_o, xor_1_out, carry_i);
  or or_1 (carry_o, and_1_out, and_2_out);
endmodule
