// Digital circuit d_flipflop_async.dig as structural Verilog
module d_flipflop_async (
  input  data_i,
  input  clk,
  input  reset_i,
  output out_o
);

  D_FF_AS flipflop (.Set(1'b0), .D(data_i), .C(clk), .Clr(reset_i), .Q(out_o));  // open: nQ
endmodule
