// Digital circuit basic_combinational_gates.dig as structural Verilog
module basic_combinational_gates (
  input  A,
  input  B,
  input  A_2,
  input  B_2,
  input  A_3,
  input  B_3,
  input  A_4,
  input  B_4,
  input  S,
  input  A_5,
  input  B_5,
  input  S0,
  input  C,
  input  D,
  input  S1,
  input  data,
  input  [1:0] selector,
  output Q,
  output Q_2,
  output Q_3,
  output out_12,
  output out_19,
  output dmux_0,
  output dmux_1,
  output dmux_2,
  output dmux_3
);

  and and_1 (Q_3, A_3, B_3);
  or or_1 (Q, A, B);
  xor xor_1 (Q_2, A_2, B_2);
  Multiplexer multiplexer_1 (.sel(S), .in_0(A_4), .in_1(B_4), .out(out_12));
  Multiplexer #(.Selector_Bits(2)) multiplexer_2 (
    .sel({S1, S0}), .in_0(A_5), .in_1(B_5), .in_2(C), .in_3(D), .out(out_19));
  Demultiplexer #(.Selector_Bits(2)) demultiplexer_1 (
    .sel(selector), .in(data), .out_0(dmux_0), .out_1(dmux_1), .out_2(dmux_2), .out_3(dmux_3));
endmodule
