// Digital circuit simple_circuit.dig as structural Verilog
module simple_circuit (
  input  in_a,
  input  in_b,
  input  in_c,
  output out_q
);

  wire and_1_out, not_1_out;

  not not_1 (not_1_out, in_a);
  and and_1 (and_1_out, not_1_out, in_b);
  or or_1 (out_q, and_1_out, in_c);
endmodule
