// Digital circuit 4bit_adder.dig as structural Verilog
module _4bit_adder (
  input  [3:0] a_i,
  input  [3:0] b_i,
  input  carry_i,
  output [3:0] sum_o
);

  wire fulladder_1_carry_o, fulladder_2_carry_o, fulladder_3_carry_o;

  fulladder fulladder_1 (
    .a_i(b_i[0]), .b_i(carry_i), .carry_i(a_i[0]), .sum_o(sum_o[0]), .carry_o(fulladder_1_carry_o));
  fulladder fulladder_2 (
    .a_i(a_i[1]), .b_i(b_i[1]), .carry_i(fulladder_1_carry_o), .sum_o(sum_o[1]), .carry_o(fulladder_2_carry_o));
  fulladder fulladder_3 (
    .a_i(a_i[2]), .b_i(b_i[2]), .carry_i(fulladder_2_carry_o), .sum_o(sum_o[2]), .carry_o(fulladder_3_carry_o));
  fulladder fulladder_4 (.a_i(a_i[3]), .b_i(b_i[3]), .carry_i(fulladder_3_carry_o), .sum_o(sum_o[3]));  // open: carry_o

  // Other names for the same wires on the sheet: a1 = a_i[0]; a2 = a_i[1]; a3 = a_i[2]; a4 = a_i[3]; b1 = b_i[0];
  //   b2 = b_i[1]; b3 = b_i[2]; b4 = b_i[3]; carry = carry_i
endmodule
