// Digital circuit mealy_fsm.dig as structural Verilog
module mealy_fsm (
  input  in_i,
  input  reset_i,
  input  clk_i,
  output out_o,
  output out_1,
  output out_2
);

  wire and_1_out, and_2_out, and_3_out, and_4_out, and_6_out, and_7_out, d_ff_as_1_q, d_ff_as_2_q, not_1_out,
       not_2_out, not_3_out, not_4_out, not_5_out, not_6_out, or_1_out, or_2_out;

  not not_1 (not_1_out, d_ff_as_1_q);
  not not_2 (not_2_out, d_ff_as_2_q);
  not not_3 (not_3_out, in_i);
  and and_1 (and_1_out, not_1_out, not_2_out, not_3_out);
  and and_2 (and_2_out, not_1_out, not_2_out, in_i);
  and and_3 (and_3_out, d_ff_as_1_q, not_2_out, in_i);
  and and_4 (and_4_out, not_1_out, d_ff_as_2_q, in_i);
  or or_1 (or_1_out, and_1_out, and_2_out);
  or or_2 (or_2_out, and_3_out, and_4_out);
  D_FF_AS d_ff_as_1 (.Set(1'b0), .D(or_1_out), .C(clk_i), .Clr(reset_i), .Q(d_ff_as_1_q));  // open: nQ
  D_FF_AS d_ff_as_2 (.Set(1'b0), .D(or_2_out), .C(clk_i), .Clr(reset_i), .Q(d_ff_as_2_q));  // open: nQ
  not not_4 (not_4_out, d_ff_as_1_q);
  not not_5 (not_5_out, d_ff_as_2_q);
  not not_6 (not_6_out, in_i);
  and and_5 (out_2, not_4_out, not_5_out);
  and and_6 (and_6_out, not_5_out, d_ff_as_1_q, not_6_out);
  and and_7 (and_7_out, not_4_out, d_ff_as_2_q, not_6_out);
  and and_8 (out_o, d_ff_as_1_q, not_5_out);
  or or_3 (out_1, and_6_out, and_7_out);
endmodule
